# Fritzing sketch omarm-zero (saved by Fritzing 1.0.6)

parts:
  J8 = Basic Servo
  J10 = Basic Servo
  J9 = Basic Servo
  JACK2 = 2.1mm Barrel Jack with Terminal Block
  Part8 = Adafruit PCA9685 PWM/Servo Breakout [part_number=815]
  U1 = ESP32-38PinWide [part_number=ESP32-38PinWide]
  M7 = Dagu DGServo 9g (Top view) [part_number=RS001B]
  M8 = Dagu DGServo 9g (Top view) [part_number=RS001B]
  M9 = Dagu DGServo 9g (Top view) [part_number=RS001B]

nets:
  GND: J8.gnd, J10.gnd, J9.gnd, JACK2.NEG, Part8.GND, U1.GND, M7.gnd, M8.gnd, M9.gnd
  VCC: J8.vcc, J10.vcc, J9.vcc, Part8.5.0V, M7.vcc, M8.vcc, M9.vcc
  N1: J8.pulse, Part8.PWM4
  N2: J10.pulse, Part8.PWM0
  N3: J9.pulse, Part8.PWM3
  N4: JACK2.POS, Part8.PWRIN
  N5: Part8.PWM7, M9.pulse
  N6: Part8.VCC, U1.3.3
  N7: Part8.SDA, U1.GPIO21
  N8: Part8.SCL, U1.GPIO22
  N9: Part8.PWM15, M7.pulse
  N10: Part8.PWM8, M8.pulse

notes:
  ESP32 wroom Bluetooth 32
  USB
  Connection
  6V
  J1
  J2
  J3
  J4
  J5
  Gripper

custom parts:
  Adafruit PCA9685 PWM/Servo Breakout: Using only two pins, control 16 free-running PWM outputs! I2C-controlled PWM driver with a built in clock. Unlike the TLC5940 family, you do not need to continuously send it signal tying up your microcontroller, its completely free running! 5V compliant, which means you can control it from a 3.3V microcontroller and still safely drive up to 6V outputs (this is good for when you want to control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
  ESP32-38PinWide: Generic 38-Pin ESP32 with wide format (only access to one side of pins on a breadboard) based on Stephen Lilley's HiLetgo ESP-WROOM-32 ESP32 ESP-32S Development Board.
